# Fritzing sketch Wiring_ESP32_BNO_NoMotor (saved by Fritzing 0.9.4)
breadboards: 1

parts:
  Part2 = Adafruit BNO085 9-DOF Orientation IMU Fusion [part_number="Addfruit #4754"]
  Part3 = Adafruit HUZZAH32 ESP32 Feather [part_number="Adafruit #3405"]
  S1 = SWITCH-MOMENTARY-2 [package=tactile-pth-12mm]
  Part4 = Lithium Ion Polymer Battery 3.7v 350mAh [part_number=2750]

nets:
  VCC: Part2.VCC, Part2.PS1, Part3.3.3V, Part4.positive
  GND: Part2.GND, Part3.GND, S1.2, Part4.negative
  N1: Part2.SCL/SCK/RX, Part3.IO17
  N2: Part2.SDA/MISO/TX, Part3.IO16
  N3: Part3.IO13_A12, S1.1

custom parts:
  Lithium Ion Polymer Battery 3.7v 350mAh: Lithium ion polymer (also known as 'lipo' or 'lipoly') batteries are thin, light and powerful. The output ranges from 4.2V when completely charged to 3.7V. This battery has a capacity of 350mAh for a total of about 1.3 Wh. The batteries come pre-attached with a genuine 2-pin JST-PH connector as shown and include the necessary protection circuitry.
