# Fritzing sketch Wiring_ESP32_BNO_WithMotor (saved by Fritzing 0.9.4)
breadboards: 1

parts:
  Part2 = Adafruit BNO085 9-DOF Orientation IMU Fusion [part_number="Addfruit #4754"]
  Part3 = Adafruit HUZZAH32 ESP32 Feather [part_number="Adafruit #3405"]
  S1 = SWITCH-MOMENTARY-2 [package=tactile-pth-12mm]
  Part4 = Lithium Ion Polymer Battery 3.7v 350mAh [part_number=2750]
  MOTOR1 = Vibration Motor
  Q1 = TRANSISTOR_NPN [package=to-92-ammo]
  D1 = Diode [package=diode-hv]
  R1 = Resistor [tolerance=±5% resistance=220 package="0805 [SMD]"]
  R2 = Resistor [tolerance=±5% resistance=220 package="0805 [SMD]"]

nets:
  VCC: Part2.VCC, Part2.PS1, Part3.3.3V, Part4.positive, MOTOR1.POS, D1.C
  GND: Part2.GND, Part3.GND, Part4.negative, Q1.E, R1.Pin_1
  N1: Part2.SCL/SCK/RX, Part3.IO17
  N2: Part2.SDA/MISO/TX, Part3.IO16
  N3: Part3.IO13_A12, S1.1
  N4: Part3.IO12_A11, R2.Pin_1
  N5: S1.2, R1.Pin_0
  N6: MOTOR1.NEG, Q1.C
  N7: Q1.B, R2.Pin_0

custom parts:
  Lithium Ion Polymer Battery 3.7v 350mAh: Lithium ion polymer (also known as 'lipo' or 'lipoly') batteries are thin, light and powerful. The output ranges from 4.2V when completely charged to 3.7V. This battery has a capacity of 350mAh for a total of about 1.3 Wh. The batteries come pre-attached with a genuine 2-pin JST-PH connector as shown and include the necessary protection circuitry.
  Vibration Motor: An eccentric vibration motor!
